# Fritzing sketch plan (saved by Fritzing 0.9.0b)
breadboards: 1

parts:
  Raspberry_Pi_B_rev1 = Raspberry Pi B rev2
  Q1 = NPN-Transistor [package="TO92 [THT]"]
  Bauteil2 = PowerBoost 1000 Basic
  Bauteil3 = Adafruit USB DC Solar LiPo Charger [part_number="Adafruit #390"]
  M1 = DC Motor
  U1 = LIPO-2000mAh [package=lipo-2000]

nets:
  N1: Raspberry_Pi_B_rev1.GPIO_2, Q1.C
  N2: Q1.E, M1.pin_2
  N3: Q1.B, Bauteil2.5.0V, Bauteil3.LOAD
  GND: Bauteil2.GND, Bauteil3.GND, M1.pin_1, U1.-
  N4: Bauteil3.BATT, U1.+

custom parts:
  PowerBoost 1000 Basic: The PowerBoost 1000 is a little DC/DC boost converter module that can run from 1.8V batteries or higher, and convert the battery output to 5.2V DC for running your 5V projects. At its heart is a TPS61030 boost converter from TI. This boost converter chip has some really nice extras such as low battery detection, 4A internal switch, synchronous conversion, excellent efficiency, and 700KHz high-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
  Adafruit USB DC Solar LiPo Charger: Make your projects to go green this summer with our specialized USB/Solar Lithium Ion Polymer Battery charger! This charger is a very unique design, perfect for outdoor projects, or DIY iPod chargers. We've spent over a year testing and tinkering with this charger to come up with a plug and play solution to charging batteries with the sun and we're really pleased with what we ended up with.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
